// Logisim project cse332_project.circ as structural Verilog
module _16bit_register_file_ic (
  input  Clock,
  input  Reset,
  input  [15:0] Write_Data,
  input  Write_Enable,
  input  [3:0] Destination__RD,
  input  [3:0] RS,
  input  [3:0] RT,
  output [15:0] Read_Data_1,
  output [15:0] Read_Data_2
);

  wire demultiplexer_1_out0, demultiplexer_1_out1, demultiplexer_1_out2, demultiplexer_1_out3,
       demultiplexer_1_out4, demultiplexer_1_out5, demultiplexer_1_out6, demultiplexer_1_out7,
       demultiplexer_1_out8, demultiplexer_1_out9, demultiplexer_1_out10, demultiplexer_1_out11,
       demultiplexer_1_out12, demultiplexer_1_out13, demultiplexer_1_out14, demultiplexer_1_out15;
  wire [15:0] r0_q, r1_q, r2_q, r3_q, r4_q, r5_q, r6_q, r7_q, r8_q, r9_q, r10_q, r11_q, r12_q, r13_q, r14_q,
       r15_q;

  Demultiplexer #(.select(4)) demultiplexer_1 (
    .out0(demultiplexer_1_out0), .out1(demultiplexer_1_out1), .out2(demultiplexer_1_out2),
    .out3(demultiplexer_1_out3), .out4(demultiplexer_1_out4), .out5(demultiplexer_1_out5),
    .out6(demultiplexer_1_out6), .out7(demultiplexer_1_out7), .out8(demultiplexer_1_out8),
    .out9(demultiplexer_1_out9), .out10(demultiplexer_1_out10), .out11(demultiplexer_1_out11),
    .out12(demultiplexer_1_out12), .out13(demultiplexer_1_out13), .out14(demultiplexer_1_out14),
    .out15(demultiplexer_1_out15), .in(Write_Enable), .sel(Destination__RD));  // open: en
  Register #(.width(16)) r0 (.D(Write_Data), .en(demultiplexer_1_out0), .Q(r0_q), .clk(Clock), .clr(Reset));
  Register #(.width(16)) r1 (.D(Write_Data), .en(demultiplexer_1_out1), .Q(r1_q), .clk(Clock), .clr(Reset));
  Register #(.width(16)) r2 (.D(Write_Data), .en(demultiplexer_1_out2), .Q(r2_q), .clk(Clock), .clr(Reset));
  Register #(.width(16)) r3 (.D(Write_Data), .en(demultiplexer_1_out3), .Q(r3_q), .clk(Clock), .clr(Reset));
  Register #(.width(16)) r4 (.D(Write_Data), .en(demultiplexer_1_out4), .Q(r4_q), .clk(Clock), .clr(Reset));
  Register #(.width(16)) r5 (.D(Write_Data), .en(demultiplexer_1_out5), .Q(r5_q), .clk(Clock), .clr(Reset));
  Register #(.width(16)) r6 (.D(Write_Data), .en(demultiplexer_1_out6), .Q(r6_q), .clk(Clock), .clr(Reset));
  Register #(.width(16)) r7 (.D(Write_Data), .en(demultiplexer_1_out7), .Q(r7_q), .clk(Clock), .clr(Reset));
  Register #(.width(16)) r8 (.D(Write_Data), .en(demultiplexer_1_out8), .Q(r8_q), .clk(Clock), .clr(Reset));
  Register #(.width(16)) r9 (.D(Write_Data), .en(demultiplexer_1_out9), .Q(r9_q), .clk(Clock), .clr(Reset));
  Register #(.width(16)) r10 (.D(Write_Data), .en(demultiplexer_1_out10), .Q(r10_q), .clk(Clock), .clr(Reset));
  Register #(.width(16)) r11 (.D(Write_Data), .en(demultiplexer_1_out11), .Q(r11_q), .clk(Clock), .clr(Reset));
  Register #(.width(16)) r12 (.D(Write_Data), .en(demultiplexer_1_out12), .Q(r12_q), .clk(Clock), .clr(Reset));
  Register #(.width(16)) r13 (.D(Write_Data), .en(demultiplexer_1_out13), .Q(r13_q), .clk(Clock), .clr(Reset));
  Register #(.width(16)) r14 (.D(Write_Data), .en(demultiplexer_1_out14), .Q(r14_q), .clk(Clock), .clr(Reset));
  Register #(.width(16)) r15 (.D(Write_Data), .en(demultiplexer_1_out15), .Q(r15_q), .clk(Clock), .clr(Reset));
  Multiplexer #(.select(4), .width(16)) multiplexer_1 (
    .in0(r0_q), .in1(r1_q), .in2(r2_q), .in3(r3_q), .in4(r4_q), .in5(r5_q), .in6(r6_q), .in7(r7_q),
    .in8(r8_q), .in9(r9_q), .in10(r10_q), .in11(r11_q), .in12(r12_q), .in13(r13_q), .in14(r14_q),
    .in15(r15_q), .out(Read_Data_1), .sel(RS));  // open: en
  Multiplexer #(.select(4), .width(16)) multiplexer_2 (
    .in0(r0_q), .in1(r1_q), .in2(r2_q), .in3(r3_q), .in4(r4_q), .in5(r5_q), .in6(r6_q), .in7(r7_q),
    .in8(r8_q), .in9(r9_q), .in10(r10_q), .in11(r11_q), .in12(r12_q), .in13(r13_q), .in14(r14_q),
    .in15(r15_q), .out(Read_Data_2), .sel(RT));  // open: en
endmodule

module _16_bit_register_file_ic_with_zero (
  input  Clock,
  input  Reset,
  input  [15:0] Write_Data,
  input  Write_Enable,
  input  [3:0] Destination__RD,
  input  [3:0] RS,
  input  [3:0] RT,
  output [15:0] Read_Data_1,
  output [15:0] Read_Data_2
);

  wire demultiplexer_1_out0, demultiplexer_1_out1, demultiplexer_1_out2, demultiplexer_1_out3,
       demultiplexer_1_out4, demultiplexer_1_out5, demultiplexer_1_out6, demultiplexer_1_out7,
       demultiplexer_1_out8, demultiplexer_1_out9, demultiplexer_1_out10, demultiplexer_1_out11,
       demultiplexer_1_out12, demultiplexer_1_out13, demultiplexer_1_out14, demultiplexer_1_out15;
  wire [15:0] s0_q, s1_q, s2_q, s3_q, s4_q, s5_q, t0_q, t1_q, t2_q, t3_q, t4_q, t5_q, t6_q, t7_q, t8_q,
       zero_q;

  Demultiplexer #(.select(4)) demultiplexer_1 (
    .out0(demultiplexer_1_out0), .out1(demultiplexer_1_out1), .out2(demultiplexer_1_out2),
    .out3(demultiplexer_1_out3), .out4(demultiplexer_1_out4), .out5(demultiplexer_1_out5),
    .out6(demultiplexer_1_out6), .out7(demultiplexer_1_out7), .out8(demultiplexer_1_out8),
    .out9(demultiplexer_1_out9), .out10(demultiplexer_1_out10), .out11(demultiplexer_1_out11),
    .out12(demultiplexer_1_out12), .out13(demultiplexer_1_out13), .out14(demultiplexer_1_out14),
    .out15(demultiplexer_1_out15), .in(Write_Enable), .sel(Destination__RD));  // open: en
  Register #(.width(16)) zero (.D({16{1'b0}}), .en(demultiplexer_1_out0), .Q(zero_q), .clk(Clock), .clr(Reset));
  Register #(.width(16)) t0 (.D(Write_Data), .en(demultiplexer_1_out1), .Q(t0_q), .clk(Clock), .clr(Reset));
  Register #(.width(16)) t1 (.D(Write_Data), .en(demultiplexer_1_out2), .Q(t1_q), .clk(Clock), .clr(Reset));
  Register #(.width(16)) t2 (.D(Write_Data), .en(demultiplexer_1_out3), .Q(t2_q), .clk(Clock), .clr(Reset));
  Register #(.width(16)) t3 (.D(Write_Data), .en(demultiplexer_1_out4), .Q(t3_q), .clk(Clock), .clr(Reset));
  Register #(.width(16)) s0 (.D(Write_Data), .en(demultiplexer_1_out5), .Q(s0_q), .clk(Clock), .clr(Reset));
  Register #(.width(16)) s1 (.D(Write_Data), .en(demultiplexer_1_out6), .Q(s1_q), .clk(Clock), .clr(Reset));
  Register #(.width(16)) s2 (.D(Write_Data), .en(demultiplexer_1_out7), .Q(s2_q), .clk(Clock), .clr(Reset));
  Register #(.width(16)) s3 (.D(Write_Data), .en(demultiplexer_1_out8), .Q(s3_q), .clk(Clock), .clr(Reset));
  Register #(.width(16)) s4 (.D(Write_Data), .en(demultiplexer_1_out9), .Q(s4_q), .clk(Clock), .clr(Reset));
  Register #(.width(16)) s5 (.D(Write_Data), .en(demultiplexer_1_out10), .Q(s5_q), .clk(Clock), .clr(Reset));
  Register #(.width(16)) t4 (.D(Write_Data), .en(demultiplexer_1_out11), .Q(t4_q), .clk(Clock), .clr(Reset));
  Register #(.width(16)) t5 (.D(Write_Data), .en(demultiplexer_1_out12), .Q(t5_q), .clk(Clock), .clr(Reset));
  Register #(.width(16)) t6 (.D(Write_Data), .en(demultiplexer_1_out13), .Q(t6_q), .clk(Clock), .clr(Reset));
  Register #(.width(16)) t7 (.D(Write_Data), .en(demultiplexer_1_out14), .Q(t7_q), .clk(Clock), .clr(Reset));
  Register #(.width(16)) t8 (.D(Write_Data), .en(demultiplexer_1_out15), .Q(t8_q), .clk(Clock), .clr(Reset));
  Multiplexer #(.select(4), .width(16)) multiplexer_1 (
    .in0(zero_q), .in1(t0_q), .in2(t1_q), .in3(t2_q), .in4(t3_q), .in5(s0_q), .in6(s1_q), .in7(s2_q),
    .in8(s3_q), .in9(s4_q), .in10(s5_q), .in11(t4_q), .in12(t5_q), .in13(t6_q), .in14(t7_q), .in15(t8_q),
    .out(Read_Data_1), .sel(RS));  // open: en
  Multiplexer #(.select(4), .width(16)) multiplexer_2 (
    .in0(zero_q), .in1(t0_q), .in2(t1_q), .in3(t2_q), .in4(t3_q), .in5(s0_q), .in6(s1_q), .in7(s2_q),
    .in8(s3_q), .in9(s4_q), .in10(s5_q), .in11(t4_q), .in12(t5_q), .in13(t6_q), .in14(t7_q), .in15(t8_q),
    .out(Read_Data_2), .sel(RT));  // open: en
endmodule

module _1bit_alu (
  input  B_prime,
  input  A,
  input  B,
  input  Cin,
  output out_5
);

  wire adder_1_out, and_1_out, or_1_out, xor_1_out, xor_2_out;

  and and_1 (and_1_out, A, B);
  or or_1 (or_1_out, A, B);
  xor xor_1 (xor_1_out, B, B_prime);
  xor xor_2 (xor_2_out, A, A);
  Adder #(.width(1)) adder_1 (.a(A), .b(xor_1_out), .out(adder_1_out), .cout(out_5));  // open: cin
  Multiplexer #(.select(3)) multiplexer_1 (
    .in0(and_1_out), .in1(or_1_out), .in2(adder_1_out), .in3(xor_2_out));  // open: in4, in5, in6, in7, out, sel, en
endmodule
